# Fritzing sketch mount (saved by Fritzing 0.9.3b)
circuit board: 2.50122cm x 2.06035cm
breadboards: 1

parts:
  U1 = ESP-12F (ESP8266 WiFi Module) [part_number=ESP8266]
  DS1 = DS18B20 1-Wire Temperature Sensor [part_number=DS18B20]
  J1 = female pin header, 2 pins [form="♀ (female)"]
  R1 = Resistor [tolerance=±5% resistance=10k package=THT]
  R2 = Resistor [tolerance=±5% resistance=10k package=THT]
  R4 = Resistor [tolerance=±5% resistance=4.7k package="0805 [SMD]"]
  R3 = Resistor [tolerance=±5% resistance=10k package="1206 [SMD]"]

nets:
  VCC: U1.VCC, DS1.VDD, J1.pin2, R1.Pin_0, R2.Pin_0, R4.Pin_0
  N1: U1.GPIO0, R2.Pin_1
  N2: U1.GPIO2, DS1.DQ, R4.Pin_1
  N3: U1.EN, R1.Pin_1
  GND: U1.GND, DS1.GND, J1.pin1, R3.Pin_0
  N4: U1.GPIO15, R3.Pin_1

notes:
  -
  +

custom parts:
  ESP-12F (ESP8266 WiFi Module): WiFi Module based on the ESP8266 with onboard PCB antenna and UART communications
