# Fritzing sketch schematics (saved by Fritzing 0.9.3b)
circuit board: 3.16611cm x 2.87549cm
breadboards: 1

parts:
  R9 = Resistor [tolerance=±5% resistance=10k package=THT]
  R11 = Resistor [tolerance=±5% resistance=10k package=THT]
  U2 = ESP8266 WiFi Module [part_number=ESP8266]
  R12 = Resistor [tolerance=±5% resistance=10k package=THT]
  S5 = Pushbutton [package=THT]
  S6 = Toggle Switch [package=THT]
  D3 = Schottky Diode [part_number=1N5817 package="300 mil [THT]"]
  R10 = Resistor [tolerance=±5% resistance=10k package=THT]

nets:
  3.3V: R9.Pin_0, R11.Pin_0, U2.VCC, R10.Pin_0
  N1: R9.Pin_1, U2.CH_PD
  N2: R11.Pin_1, U2.GPIO_0, S6.COM
  GND: U2.GND, R12.Pin_1, S5.leg0, S6.L2
  N3: U2.GPIO_15, R12.Pin_0
  N4: U2.GPIO_16, D3.anode
  N5: U2.REST, S5.leg1, D3.cathode, R10.Pin_1
